# Fritzing sketch FINAL-PROJECT-CAPACITANCE (saved by Fritzing 0.8.7b)
breadboards: 1

parts:
  Part1 = Arduino Mega ADK (Rev3)
  R2 = Resistor [tolerance=±5% resistance=220 package=THT]
  R1 = Resistor [tolerance=±5% resistance=10k package=THT]
  C1 = Tantalum Capacitor [capacitance=1μF package="100 mil [THT, tantalum]"]

nets:
  N1: Part1.A0, R2.Pin_0, R1.Pin_1, C1.+
  N2: Part1.GND, C1.-
  N3: Part1.D13_PWM, R1.Pin_0
  N4: Part1.D11_PWM, R2.Pin_1

notes:
  CAPACITANCE READING
  01 RULONA-POLIRAN
