# Fritzing sketch FINAL-PROJECT_IND (saved by Fritzing 0.8.7b)
breadboards: 1

parts:
  Part1 = Arduino Mega ADK (Rev3)
  R2 = Resistor [tolerance=±5% resistance=150 package=THT]
  D2 = Rectifier Diode [part_number=1N4001 package="300 mil [THT]"]
  L2 = Inductor [package="400 mil [THT]"]
  C2 = Capacitor [package=cap-pth-small2]
  C3 = Capacitor [package=cap-pth-small2]
  R3 = Resistor [tolerance=±5% resistance=330 package=THT]

nets:
  N1: Part1.D8_PWM, R3.Pin_1
  N2: Part1.GND, L2.pin_1, C2.1, C3.2
  N3: R2.Pin_1, D2.cathode
  N4: D2.anode, L2.pin_0, C2.2, C3.1

notes:
  01 RULONA-POLIRAN
  INDUCTANCE READING
